// Logisim project D_Flipflop.circ as structural Verilog: 1 circuit, main circuit main
module main (
  input  in_1,
  output Q1,
  output nQ1,
  output Q3,
  output nS2,
  output nQ3,
  output Q2,
  output nQ2
);

  wire clock_1_out;

  Clock clock_1 (.out(clock_1_out));
  and and_1 (nS2, nQ1, clock_1_out);
  nand nand_1 (Q1, nQ2, nQ1);
  nand nand_2 (nQ1, Q1, clock_1_out);
  nand nand_3 (Q2, nS2, nQ2);
  nand nand_4 (nQ2, Q2, in_1);
  nand nand_5 (Q3, nQ1, nQ3);
  nand nand_6 (nQ3, Q3, Q2);
endmodule
