// Logisim project D_Flipflop_and_D_Latch_comparison.circ as structural Verilog: 1 circuit, main circuit main
module main (
  input  in_1,
  input  in_2,
  input  in_3,
  output out_4,
  output out_5,
  output out_6,
  output out_7
);

  wire and_1_out, clock_1_out, nand_1_out, nand_2_out, nand_5_out, nand_6_out, nand_7_out, nand_8_out,
       not_1_out;

  Clock clock_1 (.out(clock_1_out));
  nand nand_1 (nand_1_out, in_1, in_2);
  not not_1 (not_1_out, in_2);
  nand nand_2 (nand_2_out, in_1, not_1_out);
  and and_1 (and_1_out, nand_6_out, clock_1_out);
  nand nand_3 (out_4, nand_1_out, out_5);
  nand nand_4 (out_5, out_4, nand_2_out);
  nand nand_5 (nand_5_out, nand_8_out, nand_6_out);
  nand nand_6 (nand_6_out, nand_5_out, clock_1_out);
  nand nand_7 (nand_7_out, and_1_out, nand_8_out);
  nand nand_8 (nand_8_out, nand_7_out, in_3);
  nand nand_9 (out_6, nand_6_out, out_7);
  nand nand_10 (out_7, out_6, nand_7_out);
endmodule
