// Logisim project RS_Flipflop.circ as structural Verilog: 1 circuit, main circuit main
module main (
  input  in_1,
  input  in_2,
  input  in_3,
  input  in_4,
  input  in_5,
  input  in_6,
  input  in_7,
  input  in_8,
  input  in_9,
  input  in_10,
  input  in_11,
  input  in_12,
  input  in_13,
  input  in_14,
  input  in_15,
  output out_16,
  output out_17,
  output out_18,
  output out_19,
  output out_20,
  output out_21,
  output out_22,
  output out_23,
  output out_24,
  output out_25,
  output out_26,
  output out_27,
  output out_28,
  output out_29,
  output out_30,
  output out_31,
  output out_32
);

  wire and_1_out, clock_1_out, clock_2_out, nand_4_out, nand_5_out, nand_6_out, nand_7_out, nand_8_out,
       nand_9_out, nand_10_out, nand_11_out, nand_12_out, nand_19_out, nand_20_out, not_3_out, not_4_out,
       or_1_out, or_2_out, or_3_out;

  Clock clock_1 (.out(clock_1_out));
  Clock clock_2 (.out(clock_2_out));
  nand nand_1 (out_16, in_1, out_19);
  nand nand_2 (out_19, out_16, in_4);
  nand nand_3 (out_24, out_24, in_9);
  or or_1 (or_1_out, in_7, out_23);
  or or_2 (or_2_out, out_22, in_8);
  and and_1 (and_1_out, nand_5_out, clock_1_out);
  not not_1 (out_22, or_1_out);
  not not_2 (out_23, or_2_out);
  nand nand_4 (nand_4_out, nand_7_out, nand_5_out);
  nand nand_5 (nand_5_out, nand_4_out, clock_1_out);
  nand nand_6 (nand_6_out, and_1_out, nand_7_out);
  nand nand_7 (nand_7_out, nand_6_out, in_10);
  not not_3 (not_3_out, in_12);
  nand nand_8 (nand_8_out, nand_11_out, nand_9_out);
  nand nand_9 (nand_9_out, nand_8_out, clock_2_out);
  nand nand_10 (nand_10_out, nand_9_out, nand_11_out);
  nand nand_11 (nand_11_out, nand_10_out, in_15);
  and and_2 (out_17, in_2, out_20);
  and and_3 (out_20, out_17, in_5);
  nand nand_12 (nand_12_out, in_12, in_14);
  or or_3 (or_3_out, not_3_out, in_14);
  nand nand_13 (out_25, nand_5_out, out_26);
  nand nand_14 (out_26, out_25, nand_6_out);
  nand nand_15 (out_28, nand_12_out, out_30);
  nand nand_16 (out_30, out_28, or_3_out);
  nand nand_17 (out_31, nand_9_out, out_32);
  nand nand_18 (out_32, out_31, nand_10_out);
  or or_4 (out_18, in_3, out_21);
  or or_5 (out_21, out_18, in_6);
  nand nand_19 (nand_19_out, in_11, in_13);
  not not_4 (not_4_out, in_13);
  nand nand_20 (nand_20_out, in_11, not_4_out);
  nand nand_21 (out_27, nand_19_out, out_29);
  nand nand_22 (out_29, out_27, nand_20_out);
endmodule
